# Fritzing sketch TripWire (saved by Fritzing 0.7.7b)
breadboards: 1

parts:
  Arduino1 = Arduino
  R1 = Resistor [tolerance=±5% resistance=22k package=THT]
  R2 = Photocell (LDR) [package=THT]
  R3 = Photocell (LDR) [package=THT]
  R4 = Resistor [tolerance=±5% resistance=22k package=THT]
  LED1 = LED - 5mm [color="Red (633nm)" package="5 mm [THT]"]
  LED2 = LED - 5mm [color="Red (633nm)" package="5 mm [THT]"]
  R5 = Resistor [tolerance=±5% resistance=220 package=THT]
  R6 = Resistor [tolerance=±5% resistance=220 package=THT]

nets:
  N1: Arduino1.+5V, R1.Pin_0, R4.Pin_0, R5.Pin_0, R6.Pin_0
  N2: Arduino1.GND, R2.pin_1, R3.pin_1, LED1.anode, LED2.anode
  N3: Arduino1.A0, R2.pin_0, R4.Pin_1
  N4: Arduino1.A1, R1.Pin_1, R3.pin_0
  N5: LED1.cathode, R5.Pin_1
  N6: LED2.cathode, R6.Pin_1

notes:
  Lasers
  Photocells
  -
  + ctrlm
  d
  c
  5V DV
  -2.1mm
  -+ center
  -500mA-1000mA
