# Fritzing sketch FrenchPress (saved by Fritzing 0.7.7b)
breadboards: 1

parts:
  Arduino1 = Arduino
  DI1 = 7 Segment Display
  R1 = Resistor [tolerance=±5% resistance=220 package=THT]
  R2 = Resistor [tolerance=±5% resistance=220 package=THT]
  LED1 = LED - 5mm [color="Green (565nm)" package="5 mm [THT]"]
  J1 = Piezo Speaker
  S1 = Square Pushbutton
  R3 = Resistor [tolerance=±5% resistance=220 package=THT]
  Q1 = NPN-Transistor [package="TO92 [THT]"]
  M1 = DC Motor

nets:
  N1: Arduino1.GND, R2.Pin_0, J1.pin1, R3.Pin_0, Q1.C
  N2: Arduino1.D12, Q1.B
  N3: Arduino1.D11, J1.pin2
  N4: Arduino1.D10, S1.leg1, R3.Pin_1
  N5: Arduino1.D9, DI1.Segment_DP
  N6: Arduino1.D8, DI1.Segment_C
  N7: Arduino1.D7, DI1.Segment_B
  N8: Arduino1.D6, DI1.Segment_A#10
  N9: Arduino1.D5, DI1.Segment_A#1
  N10: Arduino1.D4, DI1.Segment_F
  N11: Arduino1.D3, DI1.Segment_E
  N12: Arduino1.D2, DI1.Segment_D
  N13: Arduino1.3V3, DI1.common_cathode#3, R1.Pin_0, R1.Pin_1, S1.leg0
  N14: Arduino1.VIN, M1.pin_1
  N15: DI1.common_cathode#8, R2.Pin_1, LED1.cathode, LED1.anode
  N16: Q1.E, M1.pin_2

notes:
  5V DC Wall Adapter
  This is a fan, not a motor.
