# Fritzing sketch ParkingSensor (saved by Fritzing 0.9.4)
breadboards: 1

parts:
  Part1 = Lilypad Arduino Board
  HC-SR04_Sensor_1 = HC-SR04 Ultrasonic Distance Sensor
  LED1 = smd LED [color="Red (633nm)" package="0805 [SMD]"]
  LED3 = smd LED [color="Yellow (595nm)" package="0805 [SMD]"]
  R1 = Rotary Potentiometer (Large) [maximum_resistance=100kΩ package=THT]
  LED4 = smd LED [color="Green (560nm)" package="0805 [SMD]"]
  R2 = Resistor [tolerance=±5% resistance=220 package=THT]
  R3 = Resistor [tolerance=±5% resistance=100 package=THT]

nets:
  GND: Part1.GND, HC-SR04_Sensor_1.GND, R1.leg1, R2.Pin_0
  N1: Part1.A2, R1.wiper
  N2: Part1.D9, HC-SR04_Sensor_1.TRIG
  N3: Part1.D10, HC-SR04_Sensor_1.ECHO
  N4: Part1.D6, LED3.anode
  N5: Part1.D5, LED1.anode
  N6: Part1.D7, LED4.anode
  VCC: Part1.VCC, HC-SR04_Sensor_1.VCC, R3.Pin_1
  N7: LED1.cathode, LED3.cathode, LED4.cathode, R2.Pin_1
  N8: R1.leg2, R3.Pin_0
